// Logisim project 4bitCounter.circ as structural Verilog: 4 circuits, main circuit main
module main (
  output f,
  output g,
  output a,
  output b,
  output c,
  output d,
  output e,
  output toggle_0,
  output toggle_1,
  output toggle_2,
  output toggle_3
);

  wire clock_1_out, ClockDivider_1_divide;
  wire [3:0] BitCounter_1_fourbit;

  Clock clock_1 (.out(clock_1_out));
  ClockDivider ClockDivider_1 (.clock(clock_1_out), .divide(ClockDivider_1_divide));
  BitCounter BitCounter_1 (.load(ClockDivider_1_divide), .clock(clock_1_out), .fourbit(BitCounter_1_fourbit));
  Multiplexer7447 Multiplexer7447_1 (
    .fourbit(BitCounter_1_fourbit), .clock(clock_1_out), .a_g({e, d, c, b, a, g, f}),
    .toggle({toggle_3, toggle_2, toggle_1, toggle_0}));
endmodule

module ClockDivider (
  input  clock,
  output divide
);

  Counter #(.max('h1ff), .width(9)) counter_1 (
    .load(divide), .D(9'h33), .count(1'b1), .carry(divide), .up(1'b1), .clk(clock), .clr(1'b0));  // open: Q

  // Notes on the sheet:
  //   Clock Divider
endmodule

module BitCounter (
  input  load,
  input  clock,
  output [3:0] fourbit
);

  wire and_1_out, and_2_out, and_3_out, and_4_out;

  Counter #(.max('h1), .width(1)) counter_1 (
    .load(and_1_out), .D(1'b0), .count(load), .Q(fourbit[0]), .up(1'b1), .clk(clock), .clr(1'b0));  // open: carry
  and and_1 (and_1_out, fourbit[0], load);
  Counter #(.max('h1), .width(1)) counter_2 (
    .load(and_2_out), .D(1'b0), .count(and_1_out), .Q(fourbit[1]), .up(1'b1), .clk(clock), .clr(1'b0));  // open: carry
  and and_2 (and_2_out, fourbit[1], and_1_out);
  Counter #(.max('h1), .width(1)) counter_3 (
    .load(and_3_out), .D(1'b0), .count(and_2_out), .Q(fourbit[2]), .up(1'b1), .clk(clock), .clr(1'b0));  // open: carry
  and and_3 (and_3_out, fourbit[2], and_2_out);
  Counter #(.max('h1), .width(1)) counter_4 (
    .load(and_4_out), .D(1'b0), .count(and_3_out), .Q(fourbit[3]), .up(1'b1), .clk(clock), .clr(1'b0));  // open: carry
  and and_4 (and_4_out, fourbit[3], and_3_out);
endmodule

module Multiplexer7447 (
  input  [3:0] fourbit,
  input  clock,
  output [6:0] a_g,
  output [3:0] toggle
);

  wire counter_1_carry, multiplexer_1_out, not_1_out, not_2_out;
  wire [1:0] counter_1_q;

  Multiplexer #(.enable("false"), .select(2)) multiplexer_1 (
    .in0(fourbit[0]), .in1(fourbit[1]), .in2(fourbit[2]), .in3(fourbit[3]), .out(multiplexer_1_out),
    .sel(counter_1_q));
  Counter #(.max('h3), .width(2)) counter_1 (
    .load(counter_1_carry), .D(2'b00), .count(1'b1), .Q(counter_1_q), .carry(counter_1_carry), .up(1'b1),
    .clk(clock), .clr(1'b0));
  Multiplexer #(.enable("false"), .width(7)) multiplexer_2 (
    .in0(7'b1111101), .in1(7'b0011000), .out(a_g), .sel(multiplexer_1_out));
  not not_1 (not_1_out, counter_1_q[0]);
  not not_2 (not_2_out, counter_1_q[1]);
  and and_1 (toggle[0], not_1_out, not_2_out);
  and and_2 (toggle[1], not_2_out, counter_1_q[0]);
  and and_3 (toggle[2], counter_1_q[1], not_1_out);
  and and_4 (toggle[3], counter_1_q[0], counter_1_q[1]);
endmodule
