// Logisim project 60secTimer.circ as structural Verilog: 4 circuits, main circuit main
module main (
  input  reverse,
  input  pause,
  input  four_x,
  output f,
  output g,
  output a,
  output b,
  output c,
  output d,
  output e,
  output toggle_0,
  output toggle_1,
  output toggle_2,
  output toggle_3
);

  wire clock_1_out, ClockDivider_1_carry;
  wire [3:0] Timer_1_gsd, Timer_1_lsd;

  Clock clock_1 (.out(clock_1_out));
  Timer Timer_1 (.clock(clock_1_out), .load(ClockDivider_1_carry), .lsd(Timer_1_lsd), .gsd(Timer_1_gsd));
  ClockDivider ClockDivider_1 (
    .reverse(reverse), .pause(pause), .clock(clock_1_out), .four_x(four_x), .carry(ClockDivider_1_carry));
  Multiplexer7447 Multiplexer7447_1 (
    .lsd(Timer_1_lsd), .gsd(Timer_1_gsd), .clock(clock_1_out), .a_g_ssd({e, d, c, b, a, g, f}),
    .toggle({toggle_1, toggle_0}));

  assign toggle_2 = 1'b0;
  assign toggle_3 = 1'b0;
endmodule

module ClockDivider (
  input  reverse,
  input  pause,
  input  clock,
  input  four_x,
  output carry
);

  wire counter_1_carry, counter_2_carry, not_1_out, not_2_out;

  not not_1 (not_1_out, pause);
  not not_2 (not_2_out, reverse);
  Counter #(.max('h1ff), .width(9)) counter_1 (
    .load(counter_1_carry), .D(9'h33), .count(not_1_out), .carry(counter_1_carry), .up(not_2_out),
    .clk(clock), .clr(1'b0));  // open: Q
  Counter #(.max('h7f), .width(7)) counter_2 (
    .load(counter_2_carry), .D({7{1'b0}}), .count(not_1_out), .carry(counter_2_carry), .up(not_2_out),
    .clk(clock), .clr(1'b0));  // open: Q
  Multiplexer #(.enable("false")) multiplexer_1 (
    .in0(counter_1_carry), .in1(counter_2_carry), .out(carry), .sel(four_x));
endmodule

module Timer (
  input  clock,
  input  load,
  output [3:0] lsd,
  output [3:0] gsd
);

  wire and_1_out, and_2_out, not_1_out, not_2_out, not_3_out, not_4_out;

  Counter #(.max('hf), .width(4)) counter_1 (
    .load(and_1_out), .D(4'b0000), .count(load), .Q(lsd), .up(1'b1), .clk(clock), .clr(1'b0));  // open: carry
  not not_1 (not_1_out, lsd[2]);
  and and_1 (and_1_out, lsd[3], not_1_out, lsd[1], not_3_out);
  Counter #(.max('hf), .width(4)) counter_2 (
    .load(and_2_out), .D(4'b0000), .count(and_1_out), .Q(gsd), .up(1'b1), .clk(clock), .clr(1'b0));  // open: carry
  not not_2 (not_2_out, gsd[3]);
  and and_2 (and_2_out, not_2_out, gsd[2], gsd[1], not_4_out);
  not not_3 (not_3_out, lsd[0]);
  not not_4 (not_4_out, gsd[0]);
endmodule

module Multiplexer7447 (
  input  [3:0] lsd,
  input  [3:0] gsd,
  input  clock,
  output [6:0] a_g_ssd,
  output [1:0] toggle
);

  wire n7447_1_pin3;
  wire [6:0] n7447_1_pin15, n7447_2_pin15;

  _7447 #(.ShowInternalStructure("true")) u_7447_1 (
    .pin1(lsd[1]), .pin2(lsd[2]), .pin3(n7447_1_pin3), .pin4(n7447_1_pin3), .pin5(n7447_1_pin3),
    .pin6(lsd[3]), .pin7(lsd[0]), .pin15(n7447_1_pin15[0]), .pin14(n7447_1_pin15[1]),
    .pin13(n7447_1_pin15[2]), .pin12(n7447_1_pin15[3]), .pin11(n7447_1_pin15[4]), .pin10(n7447_1_pin15[5]),
    .pin9(n7447_1_pin15[6]));
  _7447 #(.ShowInternalStructure("true")) u_7447_2 (
    .pin1(gsd[1]), .pin2(gsd[2]), .pin3(n7447_1_pin3), .pin4(n7447_1_pin3), .pin5(n7447_1_pin3),
    .pin6(gsd[3]), .pin7(gsd[0]), .pin15(n7447_2_pin15[0]), .pin14(n7447_2_pin15[1]),
    .pin13(n7447_2_pin15[2]), .pin12(n7447_2_pin15[3]), .pin11(n7447_2_pin15[4]), .pin10(n7447_2_pin15[5]),
    .pin9(n7447_2_pin15[6]));
  Multiplexer #(.enable("false"), .width(7)) multiplexer_1 (
    .in0(n7447_1_pin15), .in1(n7447_2_pin15), .out(a_g_ssd), .sel(clock));
  not not_1 (toggle[0], clock);

  assign toggle[1] = clock;
  // also tied to VCC on the sheet: n7447_1_pin3
endmodule
