// Logisim project 60secTimerTwo.circ as structural Verilog: 4 circuits, main circuit main
module main (
  input  reverse,
  input  pause,
  input  four_x,
  output f,
  output g,
  output a,
  output b,
  output c,
  output d,
  output e,
  output toggle_0,
  output toggle_1,
  output toggle_2,
  output toggle_3
);

  wire clock_1_out, ClockDivider_1_carry;
  wire [3:0] Timer_1_gsd, Timer_1_lsd;

  Clock clock_1 (.out(clock_1_out));
  Timer Timer_1 (
    .reverse(reverse), .by_2(1'b0), .clock(clock_1_out), .load(ClockDivider_1_carry), .lsd(Timer_1_lsd),
    .gsd(Timer_1_gsd));
  ClockDivider ClockDivider_1 (.pause(pause), .clock(clock_1_out), .four_x(four_x), .carry(ClockDivider_1_carry));
  Multiplexer7447 Multiplexer7447_1 (
    .lsd(Timer_1_lsd), .gsd(Timer_1_gsd), .clock(clock_1_out), .a_g_ssd({e, d, c, b, a, g, f}),
    .toggle({toggle_1, toggle_0}));

  assign toggle_2 = 1'b0;
  assign toggle_3 = 1'b0;
endmodule

module ClockDivider (
  input  pause,
  input  clock,
  input  four_x,
  output carry
);

  wire counter_1_carry, counter_2_carry, not_1_out;

  not not_1 (not_1_out, pause);
  Counter #(.max('h1ff), .width(9)) counter_1 (
    .load(counter_1_carry), .D(9'h33), .count(not_1_out), .carry(counter_1_carry), .up(1'b1), .clk(clock),
    .clr(1'b0));  // open: Q
  Counter #(.max('h7f), .width(7)) counter_2 (
    .load(counter_2_carry), .D({7{1'b0}}), .count(not_1_out), .carry(counter_2_carry), .up(1'b1),
    .clk(clock), .clr(1'b0));  // open: Q
  Multiplexer #(.enable("false")) multiplexer_1 (
    .in0(counter_1_carry), .in1(counter_2_carry), .out(carry), .sel(four_x));

  // Notes on the sheet:
  //   Clock Divider
endmodule

module Timer (
  input  reverse,
  input  by_2,
  input  clock,
  input  load,
  output [3:0] lsd,
  output [3:0] gsd
);

  wire and_1_out, and_2_out, and_3_out, and_4_out, and_5_out, multiplexer_2_out, multiplexer_4_out,
       not_2_out, not_3_out, not_4_out, not_5_out, not_6_out, not_7_out, not_8_out, not_9_out, not_10_out,
       not_11_out, not_12_out, not_14_out, not_15_out, not_16_out, not_17_out;
  wire [0:0] not_1_out;
  wire [3:0] adder_1_out, counter_1_q, multiplexer_1_out, multiplexer_3_out;

  not not_1 (not_1_out[0], reverse);
  Adder #(.width(4)) adder_1 (.a(counter_1_q), .b(counter_1_q), .out(adder_1_out), .cin(1'b0));  // open: cout
  Counter #(.max('hf), .width(4)) counter_1 (
    .load(multiplexer_2_out), .D(multiplexer_1_out), .count(load), .Q(counter_1_q), .up(not_1_out[0]),
    .clk(clock), .clr(1'b0));  // open: carry
  Multiplexer #(.enable("false"), .select(2), .width(4)) multiplexer_1 (
    .in0(4'b0000), .in1(4'b1001), .in2(4'b0100), .in3(4'b0000), .out(multiplexer_1_out),
    .sel({by_2, not_1_out[0]}));
  Multiplexer #(.enable("false"), .select(2)) multiplexer_2 (
    .in0(and_2_out), .in1(and_4_out), .in2(and_2_out), .in3(and_5_out), .out(multiplexer_2_out),
    .sel({by_2, not_1_out[0]}));
  Multiplexer #(.enable("false"), .width(4)) multiplexer_3 (
    .in0(4'b0101), .in1(4'b0000), .out(multiplexer_3_out), .sel(not_1_out[0]));
  Counter #(.max('hf), .width(4)) counter_2 (
    .load(multiplexer_4_out), .D(multiplexer_3_out), .count(multiplexer_2_out), .Q(gsd), .up(not_1_out[0]),
    .clk(clock), .clr(1'b0));  // open: carry
  not not_2 (not_2_out, gsd[3]);
  and and_1 (and_1_out, not_2_out, gsd[2], load, not_6_out, gsd[0]);
  Multiplexer #(.enable("false")) multiplexer_4 (
    .in0(and_3_out), .in1(and_1_out), .out(multiplexer_4_out), .sel(not_1_out[0]));
  not not_3 (not_3_out, counter_1_q[3]);
  not not_4 (not_4_out, counter_1_q[2]);
  not not_5 (not_5_out, counter_1_q[1]);
  and and_2 (and_2_out, load, not_3_out, not_4_out, not_5_out, not_12_out);
  not not_6 (not_6_out, gsd[1]);
  not not_7 (not_7_out, gsd[0]);
  not not_8 (not_8_out, gsd[1]);
  not not_9 (not_9_out, gsd[2]);
  not not_10 (not_10_out, gsd[3]);
  and and_3 (and_3_out, not_7_out, not_8_out, load, not_9_out, not_10_out);
  not not_11 (not_11_out, by_2);
  Multiplexer #(.enable("false"), .width(4)) multiplexer_5 (
    .in0(adder_1_out), .in1(counter_1_q), .out(lsd), .sel(not_11_out));
  not not_12 (not_12_out, counter_1_q[0]);
  // NOT_Gate not_13 has open pins: in=counter_1_q[2], out=open
  not not_14 (not_14_out, counter_1_q[1]);
  and and_4 (and_4_out, load, counter_1_q[3], not_14_out, counter_1_q[0]);
  not not_15 (not_15_out, counter_1_q[3]);
  not not_16 (not_16_out, counter_1_q[1]);
  not not_17 (not_17_out, counter_1_q[0]);
  and and_5 (and_5_out, load, not_15_out, counter_1_q[2], not_16_out, not_17_out);

  // Notes on the sheet:
  //   Timer
endmodule

module Multiplexer7447 (
  input  [3:0] lsd,
  input  [3:0] gsd,
  input  clock,
  output [6:0] a_g_ssd,
  output [1:0] toggle
);

  wire n7447_1_pin3;
  wire [6:0] n7447_1_pin15, n7447_2_pin15;

  _7447 #(.ShowInternalStructure("true")) u_7447_1 (
    .pin1(lsd[1]), .pin2(lsd[2]), .pin3(n7447_1_pin3), .pin4(n7447_1_pin3), .pin5(n7447_1_pin3),
    .pin6(lsd[3]), .pin7(lsd[0]), .pin15(n7447_1_pin15[0]), .pin14(n7447_1_pin15[1]),
    .pin13(n7447_1_pin15[2]), .pin12(n7447_1_pin15[3]), .pin11(n7447_1_pin15[4]), .pin10(n7447_1_pin15[5]),
    .pin9(n7447_1_pin15[6]));
  _7447 #(.ShowInternalStructure("true")) u_7447_2 (
    .pin1(gsd[1]), .pin2(gsd[2]), .pin3(n7447_1_pin3), .pin4(n7447_1_pin3), .pin5(n7447_1_pin3),
    .pin6(gsd[3]), .pin7(gsd[0]), .pin15(n7447_2_pin15[0]), .pin14(n7447_2_pin15[1]),
    .pin13(n7447_2_pin15[2]), .pin12(n7447_2_pin15[3]), .pin11(n7447_2_pin15[4]), .pin10(n7447_2_pin15[5]),
    .pin9(n7447_2_pin15[6]));
  Multiplexer #(.enable("false"), .width(7)) multiplexer_1 (
    .in0(n7447_1_pin15), .in1(n7447_2_pin15), .out(a_g_ssd), .sel(clock));
  not not_1 (toggle[0], clock);

  assign toggle[1] = clock;
  // also tied to VCC on the sheet: n7447_1_pin3

  // Notes on the sheet:
  //   Multiplexer/7447
endmodule
