// Logisim project 8BitAdder.circ as structural Verilog: 3 circuits, main circuit main
module main (
  input  in_1
);

  wire adder_1_cout, adder_1_out, adder_2_cout, adder_2_out, adder_3_cout, adder_3_out, adder_4_cout,
       adder_4_out, adder_5_cout, adder_6_cout, n7447_1_pin3, n7447_1_pin9, n7447_1_pin10, n7447_1_pin11,
       n7447_1_pin12, n7447_1_pin13, n7447_1_pin14, n7447_1_pin15;
  wire [6:0] dipswitch_1_sw8, dipswitch_2_sw8;

  DipSwitch dipswitch_1 (
    .sw2(dipswitch_1_sw8[6]), .sw3(dipswitch_1_sw8[5]), .sw4(dipswitch_1_sw8[4]), .sw5(dipswitch_1_sw8[3]),
    .sw6(dipswitch_1_sw8[2]), .sw7(dipswitch_1_sw8[1]), .sw8(dipswitch_1_sw8[0]));  // open: sw1
  DipSwitch dipswitch_2 (
    .sw2(dipswitch_2_sw8[6]), .sw3(dipswitch_2_sw8[5]), .sw4(dipswitch_2_sw8[4]), .sw5(dipswitch_2_sw8[3]),
    .sw6(dipswitch_2_sw8[2]), .sw7(dipswitch_2_sw8[1]), .sw8(dipswitch_2_sw8[0]));  // open: sw1
  Adder #(.width(1)) adder_1 (
    .a(dipswitch_1_sw8[0]), .b(dipswitch_2_sw8[0]), .out(adder_1_out), .cout(adder_1_cout));  // open: cin
  Adder #(.width(1)) adder_2 (
    .a(dipswitch_1_sw8[1]), .b(dipswitch_2_sw8[1]), .out(adder_2_out), .cin(adder_1_cout), .cout(adder_2_cout));
  Adder #(.width(1)) adder_3 (
    .a(dipswitch_1_sw8[2]), .b(dipswitch_2_sw8[2]), .out(adder_3_out), .cin(adder_2_cout), .cout(adder_3_cout));
  Adder #(.width(1)) adder_4 (
    .a(dipswitch_1_sw8[3]), .b(dipswitch_2_sw8[3]), .out(adder_4_out), .cin(adder_3_cout), .cout(adder_4_cout));
  Adder #(.width(1)) adder_5 (
    .a(dipswitch_1_sw8[4]), .b(dipswitch_2_sw8[4]), .cin(adder_4_cout), .cout(adder_5_cout));  // open: out
  Adder #(.width(1)) adder_6 (
    .a(dipswitch_1_sw8[5]), .b(dipswitch_2_sw8[5]), .cin(adder_5_cout), .cout(adder_6_cout));  // open: out
  Adder #(.width(1)) adder_7 (.a(dipswitch_1_sw8[6]), .b(dipswitch_2_sw8[6]), .cin(adder_6_cout));  // open: out, cout
  _7447 #(.ShowInternalStructure("true")) u_7447_1 (
    .pin1(adder_2_out), .pin2(adder_3_out), .pin3(n7447_1_pin3), .pin4(n7447_1_pin3), .pin5(n7447_1_pin3),
    .pin6(adder_4_out), .pin7(adder_1_out), .pin15(n7447_1_pin15), .pin14(n7447_1_pin14),
    .pin13(n7447_1_pin13), .pin12(n7447_1_pin12), .pin11(n7447_1_pin11), .pin10(n7447_1_pin10),
    .pin9(n7447_1_pin9));
  _7_Segment_Display #(.decimalPoint("false")) PosNeg ();  // open: g, f, a, b, e, d, c
  _7_Segment_Display #(.decimalPoint("false")) LSDigit (
    .g(n7447_1_pin14), .f(n7447_1_pin15), .a(n7447_1_pin13), .b(n7447_1_pin12), .e(n7447_1_pin9),
    .d(n7447_1_pin10), .c(n7447_1_pin11));
  // also tied to VCC on the sheet: n7447_1_pin3

  // Notes on the sheet:
  //   Add == 0 / Sub==1
endmodule

module changed (
  input  in_1
);

  wire adder_1_cout, adder_1_out, adder_2_cout, adder_2_out, adder_3_cout, adder_3_out, adder_4_cout,
       adder_4_out, adder_5_cout, adder_5_out, adder_6_cout, adder_6_out, adder_7_cout, adder_7_out,
       adder_8_out, adder_9_cout, adder_9_out, adder_10_cout, adder_10_out, adder_11_cout, adder_11_out,
       adder_12_out, n7447_1_pin3, n7447_1_pin9, n7447_1_pin10, n7447_1_pin11, n7447_1_pin12, n7447_1_pin13,
       n7447_1_pin14, n7447_1_pin15, xor_1_out, xor_2_out, xor_3_out, xor_4_out, xor_5_out, xor_6_out,
       xor_7_out, xor_8_out, xor_9_out, xor_10_out, xor_11_out, xor_12_out;
  wire [7:0] dipswitch_1_sw8, dipswitch_2_sw8;

  DipSwitch dipswitch_1 (
    .sw1(dipswitch_1_sw8[7]), .sw2(dipswitch_1_sw8[6]), .sw3(dipswitch_1_sw8[5]), .sw4(dipswitch_1_sw8[4]),
    .sw5(dipswitch_1_sw8[3]), .sw6(dipswitch_1_sw8[2]), .sw7(dipswitch_1_sw8[1]), .sw8(dipswitch_1_sw8[0]));
  DipSwitch dipswitch_2 (
    .sw1(dipswitch_2_sw8[7]), .sw2(dipswitch_2_sw8[6]), .sw3(dipswitch_2_sw8[5]), .sw4(dipswitch_2_sw8[4]),
    .sw5(dipswitch_2_sw8[3]), .sw6(dipswitch_2_sw8[2]), .sw7(dipswitch_2_sw8[1]), .sw8(dipswitch_2_sw8[0]));
  LED led_1 (.in(adder_8_out));
  xor xor_1 (xor_1_out, dipswitch_2_sw8[0], in_1);
  xor xor_2 (xor_2_out, dipswitch_2_sw8[1], in_1);
  xor xor_3 (xor_3_out, dipswitch_2_sw8[2], in_1);
  xor xor_4 (xor_4_out, dipswitch_2_sw8[3], in_1);
  xor xor_5 (xor_5_out, dipswitch_2_sw8[4], in_1);
  xor xor_6 (xor_6_out, dipswitch_2_sw8[5], in_1);
  xor xor_7 (xor_7_out, dipswitch_2_sw8[6], in_1);
  xor xor_8 (xor_8_out, dipswitch_2_sw8[7], in_1);
  LED led_2 (.in(adder_7_out));
  LED led_3 (.in(adder_6_out));
  LED led_4 (.in(adder_5_out));
  LED led_5 (.in(adder_4_out));
  Adder #(.width(1)) adder_1 (
    .a(dipswitch_1_sw8[0]), .b(xor_1_out), .out(adder_1_out), .cin(in_1), .cout(adder_1_cout));
  Adder #(.width(1)) adder_2 (
    .a(dipswitch_1_sw8[1]), .b(xor_2_out), .out(adder_2_out), .cin(adder_1_cout), .cout(adder_2_cout));
  Adder #(.width(1)) adder_3 (
    .a(dipswitch_1_sw8[2]), .b(xor_3_out), .out(adder_3_out), .cin(adder_2_cout), .cout(adder_3_cout));
  Adder #(.width(1)) adder_4 (
    .a(dipswitch_1_sw8[3]), .b(xor_4_out), .out(adder_4_out), .cin(adder_3_cout), .cout(adder_4_cout));
  Adder #(.width(1)) adder_5 (
    .a(dipswitch_1_sw8[4]), .b(xor_5_out), .out(adder_5_out), .cin(adder_4_cout), .cout(adder_5_cout));
  Adder #(.width(1)) adder_6 (
    .a(dipswitch_1_sw8[5]), .b(xor_6_out), .out(adder_6_out), .cin(adder_5_cout), .cout(adder_6_cout));
  Adder #(.width(1)) adder_7 (
    .a(dipswitch_1_sw8[6]), .b(xor_7_out), .out(adder_7_out), .cin(adder_6_cout), .cout(adder_7_cout));
  Adder #(.width(1)) adder_8 (
    .a(dipswitch_1_sw8[7]), .b(xor_8_out), .out(adder_8_out), .cin(adder_7_cout));  // open: cout
  LED led_6 (.in(adder_3_out));
  LED led_7 (.in(adder_2_out));
  LED led_8 (.in(adder_1_out));
  xor xor_9 (xor_9_out, adder_1_out, adder_8_out);
  Adder #(.width(1)) adder_9 (.a(xor_9_out), .b(adder_8_out), .out(adder_9_out), .cout(adder_9_cout));  // open: cin
  xor xor_10 (xor_10_out, adder_2_out, adder_8_out);
  Adder #(.width(1)) adder_10 (.a(1'b0), .b(xor_10_out), .out(adder_10_out), .cin(adder_9_cout), .cout(adder_10_cout));
  xor xor_11 (xor_11_out, adder_3_out, adder_8_out);
  Adder #(.width(1)) adder_11 (.a(1'b0), .b(xor_11_out), .out(adder_11_out), .cin(adder_10_cout), .cout(adder_11_cout));
  xor xor_12 (xor_12_out, adder_4_out, adder_8_out);
  Adder #(.width(1)) adder_12 (.a(1'b0), .b(xor_12_out), .out(adder_12_out), .cin(adder_11_cout));  // open: cout
  _7447 #(.ShowInternalStructure("true")) u_7447_1 (
    .pin1(adder_10_out), .pin2(adder_11_out), .pin3(n7447_1_pin3), .pin4(n7447_1_pin3), .pin5(n7447_1_pin3),
    .pin6(adder_12_out), .pin7(adder_9_out), .pin15(n7447_1_pin15), .pin14(n7447_1_pin14),
    .pin13(n7447_1_pin13), .pin12(n7447_1_pin12), .pin11(n7447_1_pin11), .pin10(n7447_1_pin10),
    .pin9(n7447_1_pin9));
  _7_Segment_Display u_7_segment_display_1 (.g(adder_8_out));  // open: f, a, b, e, d, c, dp
  _7_Segment_Display u_7_segment_display_2 (
    .g(n7447_1_pin14), .f(n7447_1_pin15), .a(n7447_1_pin13), .b(n7447_1_pin12), .e(n7447_1_pin9),
    .d(n7447_1_pin10), .c(n7447_1_pin11));  // open: dp
  // also tied to VCC on the sheet: n7447_1_pin3
endmodule

module tryingagain (
  input  in_1
);

  wire adder_1_cout, adder_1_out, adder_2_cout, adder_2_out, adder_3_cout, adder_3_out, adder_4_cout,
       adder_4_out, adder_5_cout, adder_6_cout, adder_7_out, n7447_1_pin3, n7447_1_pin9, n7447_1_pin10,
       n7447_1_pin11, n7447_1_pin12, n7447_1_pin13, n7447_1_pin14, n7447_1_pin15, xor_1_out, xor_2_out,
       xor_3_out, xor_4_out, xor_5_out, xor_6_out, xor_7_out;
  wire [6:0] dipswitch_1_sw8, dipswitch_2_sw8;

  DipSwitch dipswitch_1 (
    .sw2(dipswitch_1_sw8[6]), .sw3(dipswitch_1_sw8[5]), .sw4(dipswitch_1_sw8[4]), .sw5(dipswitch_1_sw8[3]),
    .sw6(dipswitch_1_sw8[2]), .sw7(dipswitch_1_sw8[1]), .sw8(dipswitch_1_sw8[0]));  // open: sw1
  DipSwitch dipswitch_2 (
    .sw2(dipswitch_2_sw8[6]), .sw3(dipswitch_2_sw8[5]), .sw4(dipswitch_2_sw8[4]), .sw5(dipswitch_2_sw8[3]),
    .sw6(dipswitch_2_sw8[2]), .sw7(dipswitch_2_sw8[1]), .sw8(dipswitch_2_sw8[0]));  // open: sw1
  xor xor_1 (xor_1_out, dipswitch_1_sw8[0], in_1);
  xor xor_2 (xor_2_out, dipswitch_1_sw8[1], in_1);
  xor xor_3 (xor_3_out, dipswitch_1_sw8[2], in_1);
  xor xor_4 (xor_4_out, dipswitch_1_sw8[3], in_1);
  xor xor_5 (xor_5_out, dipswitch_1_sw8[4], in_1);
  xor xor_6 (xor_6_out, dipswitch_1_sw8[5], in_1);
  xor xor_7 (xor_7_out, dipswitch_1_sw8[6], in_1);
  Adder #(.width(1)) adder_1 (
    .a(dipswitch_2_sw8[0]), .b(xor_1_out), .out(adder_1_out), .cin(in_1), .cout(adder_1_cout));
  Adder #(.width(1)) adder_2 (
    .a(dipswitch_2_sw8[1]), .b(xor_2_out), .out(adder_2_out), .cin(adder_1_cout), .cout(adder_2_cout));
  Adder #(.width(1)) adder_3 (
    .a(dipswitch_2_sw8[2]), .b(xor_3_out), .out(adder_3_out), .cin(adder_2_cout), .cout(adder_3_cout));
  Adder #(.width(1)) adder_4 (
    .a(dipswitch_2_sw8[3]), .b(xor_4_out), .out(adder_4_out), .cin(adder_3_cout), .cout(adder_4_cout));
  Adder #(.width(1)) adder_5 (
    .a(dipswitch_2_sw8[4]), .b(xor_5_out), .cin(adder_4_cout), .cout(adder_5_cout));  // open: out
  Adder #(.width(1)) adder_6 (
    .a(dipswitch_2_sw8[5]), .b(xor_6_out), .cin(adder_5_cout), .cout(adder_6_cout));  // open: out
  Adder #(.width(1)) adder_7 (
    .a(dipswitch_2_sw8[6]), .b(xor_7_out), .out(adder_7_out), .cin(adder_6_cout));  // open: cout
  _7447 #(.ShowInternalStructure("true")) u_7447_1 (
    .pin1(adder_2_out), .pin2(adder_3_out), .pin3(n7447_1_pin3), .pin4(n7447_1_pin3), .pin5(n7447_1_pin3),
    .pin6(adder_4_out), .pin7(adder_1_out), .pin15(n7447_1_pin15), .pin14(n7447_1_pin14),
    .pin13(n7447_1_pin13), .pin12(n7447_1_pin12), .pin11(n7447_1_pin11), .pin10(n7447_1_pin10),
    .pin9(n7447_1_pin9));
  _7_Segment_Display u_7_segment_display_1 (.g(adder_7_out));  // open: f, a, b, e, d, c, dp
  _7_Segment_Display u_7_segment_display_2 (
    .g(n7447_1_pin14), .f(n7447_1_pin15), .a(n7447_1_pin13), .b(n7447_1_pin12), .e(n7447_1_pin9),
    .d(n7447_1_pin10), .c(n7447_1_pin11));  // open: dp
  // also tied to VCC on the sheet: n7447_1_pin3
endmodule
