// Logisim project BinaryAdder.circ as structural Verilog: 2 circuits, main circuit main
module main (
  input  x0,
  input  x1,
  input  x2,
  input  y0,
  input  y1,
  input  y2
);

  wire and_1_out, and_2_out, and_3_out, and_4_out, and_5_out, and_6_out, and_7_out, n7447_1_pin3,
       n7447_1_pin9, n7447_1_pin10, n7447_1_pin11, n7447_1_pin12, n7447_1_pin13, n7447_1_pin14,
       n7447_1_pin15, or_1_out, or_2_out, or_3_out, or_4_out, xor_1_out, xor_2_out, xor_3_out, xor_4_out,
       xor_5_out;

  xor xor_1 (xor_1_out, y2, x2);
  xor xor_2 (xor_2_out, x0, y0);
  and and_1 (and_1_out, x0, y0);
  and and_2 (and_2_out, x1, y1);
  and and_3 (and_3_out, and_1_out, y1);
  and and_4 (and_4_out, and_1_out, x1);
  and and_5 (and_5_out, y1, x1);
  and and_6 (and_6_out, x2, y2);
  and and_7 (and_7_out, and_1_out, x2);
  xor xor_3 (xor_3_out, x1, y1);
  or or_1 (or_1_out, and_3_out, and_4_out);
  or or_2 (or_2_out, and_6_out, and_7_out);
  xor xor_4 (xor_4_out, and_1_out, xor_3_out);
  xor xor_5 (xor_5_out, xor_1_out, and_2_out);
  or or_3 (or_3_out, or_1_out, and_5_out);
  LED led_1 (.in(or_4_out));
  LED led_2 (.in(xor_4_out));
  or or_4 (or_4_out, xor_5_out, or_3_out);
  LED led_3 (.in(xor_2_out));
  LED led_4 ();  // open: in
  _7447 #(.ShowInternalStructure("true")) u_7447_1 (
    .pin1(xor_4_out), .pin2(or_4_out), .pin3(n7447_1_pin3), .pin4(n7447_1_pin3), .pin5(n7447_1_pin3),
    .pin6(or_2_out), .pin7(xor_2_out), .pin15(n7447_1_pin15), .pin14(n7447_1_pin14), .pin13(n7447_1_pin13),
    .pin12(n7447_1_pin12), .pin11(n7447_1_pin11), .pin10(n7447_1_pin10), .pin9(n7447_1_pin9));
  _7_Segment_Display u_7_segment_display_1 (
    .g(n7447_1_pin14), .f(n7447_1_pin15), .a(n7447_1_pin13), .b(n7447_1_pin12), .e(n7447_1_pin9),
    .d(n7447_1_pin10), .c(n7447_1_pin11));  // open: dp
  // also tied to VCC on the sheet: n7447_1_pin3
endmodule

module HalfAdderCircuit (
  input  x0,
  input  x1,
  input  x2,
  input  x3,
  input  y0,
  input  y1,
  input  y2,
  input  y3
);

  wire adder_1_cout, adder_1_out, adder_2_cout, adder_2_out, adder_3_cout, adder_3_out, adder_4_out,
       n7447_1_pin3, n7447_1_pin9, n7447_1_pin10, n7447_1_pin11, n7447_1_pin12, n7447_1_pin13, n7447_1_pin14,
       n7447_1_pin15;

  Adder #(.width(1)) adder_1 (.a(x0), .b(y0), .out(adder_1_out), .cout(adder_1_cout));  // open: cin
  Adder #(.width(1)) adder_2 (.a(x1), .b(y1), .out(adder_2_out), .cin(adder_1_cout), .cout(adder_2_cout));
  Adder #(.width(1)) adder_3 (.a(x2), .b(y2), .out(adder_3_out), .cin(adder_2_cout), .cout(adder_3_cout));
  Adder #(.width(1)) adder_4 (.a(x3), .b(y3), .out(adder_4_out), .cin(adder_3_cout));  // open: cout
  _7447 #(.ShowInternalStructure("true")) u_7447_1 (
    .pin1(adder_2_out), .pin2(adder_3_out), .pin3(n7447_1_pin3), .pin4(n7447_1_pin3), .pin5(n7447_1_pin3),
    .pin6(adder_4_out), .pin7(adder_1_out), .pin15(n7447_1_pin15), .pin14(n7447_1_pin14),
    .pin13(n7447_1_pin13), .pin12(n7447_1_pin12), .pin11(n7447_1_pin11), .pin10(n7447_1_pin10),
    .pin9(n7447_1_pin9));
  _7_Segment_Display u_7_segment_display_1 (
    .g(n7447_1_pin14), .f(n7447_1_pin15), .a(n7447_1_pin13), .b(n7447_1_pin12), .e(n7447_1_pin9),
    .d(n7447_1_pin10), .c(n7447_1_pin11));  // open: dp
  // also tied to VCC on the sheet: n7447_1_pin3
endmodule
