// Logisim project Circuit.circ as structural Verilog: 1 circuit, main circuit main
module main (
);

  wire and_1_out, or_1_out, undriven, undriven_2, undriven_3;

  or or_1 (or_1_out, undriven, undriven_2);
  and and_1 (and_1_out, undriven_2, undriven_3);
  // AND_Gate and_2 has open pins: in0=or_1_out, in1=and_1_out, out=open
endmodule
