// Logisim project DFF_Counter.circ as structural Verilog: 2 circuits, main circuit main
module main (
  output Out_3,
  output Out_2,
  output Out_1,
  output Out_0
);

  wire and_1_out, and_2_out, clock_1_out, d_ff_1_qn, xor_1_out, xor_2_out, xor_3_out;

  Clock clock_1 (.out(clock_1_out));
  D_Flip_Flop d_ff_1 (.D(d_ff_1_qn), .clk(clock_1_out), .Q(Out_0), .Qn(d_ff_1_qn));  // open: preset, reset
  and and_1 (and_1_out, Out_0, Out_1);
  and and_2 (and_2_out, Out_2, and_1_out);
  D_Flip_Flop d_ff_2 (.D(xor_3_out), .clk(clock_1_out), .Q(Out_1));  // open: Qn, preset, reset
  xor xor_1 (xor_1_out, Out_3, and_2_out);
  xor xor_2 (xor_2_out, Out_2, and_1_out);
  xor xor_3 (xor_3_out, Out_0, Out_1);
  D_Flip_Flop d_ff_3 (.D(xor_2_out), .clk(clock_1_out), .Q(Out_2));  // open: Qn, preset, reset
  D_Flip_Flop d_ff_4 (.D(xor_1_out), .clk(clock_1_out), .Q(Out_3));  // open: Qn, preset, reset
endmodule

module Base (
  output Out_2,
  output Out_1,
  output Out_0
);

  wire and_1_out, and_2_out, and_3_out, clock_1_out, d_ff_1_qn, d_ff_2_qn, d_ff_3_qn, or_1_out, xor_1_out;

  Clock clock_1 (.out(clock_1_out));
  D_Flip_Flop d_ff_1 (.D(d_ff_1_qn), .clk(clock_1_out), .Q(Out_0), .Qn(d_ff_1_qn));  // open: preset, reset
  and and_1 (and_1_out, Out_2, d_ff_2_qn);
  and and_2 (and_2_out, Out_2, d_ff_1_qn);
  and and_3 (and_3_out, d_ff_3_qn, Out_0, Out_1);
  D_Flip_Flop d_ff_2 (.D(xor_1_out), .clk(clock_1_out), .Q(Out_1), .Qn(d_ff_2_qn));  // open: preset, reset
  or or_1 (or_1_out, and_1_out, and_2_out, and_3_out);
  xor xor_1 (xor_1_out, Out_0, Out_1);
  D_Flip_Flop d_ff_3 (.D(or_1_out), .clk(clock_1_out), .Q(Out_2), .Qn(d_ff_3_qn));  // open: preset, reset
endmodule
