// Logisim project DeMorgan1.circ as structural Verilog: 1 circuit, main circuit main
module main (
  input  VinA,
  input  VinB,
  input  VinC,
  output out_4
);

  wire and_1_out, and_2_out, and_3_out, and_4_out, not_1_out, not_2_out, not_3_out, or_1_out;

  not not_1 (not_1_out, VinA);
  not not_2 (not_2_out, VinC);
  not not_3 (not_3_out, VinB);
  and and_1 (and_1_out, VinB, VinC);
  and and_2 (and_2_out, not_1_out, VinB);
  and and_3 (and_3_out, and_2_out, not_2_out);
  and and_4 (and_4_out, VinA, or_1_out);
  or or_1 (or_1_out, not_3_out, and_1_out);
  or or_2 (out_4, and_3_out, and_4_out);
endmodule
