// Logisim project DeMorganNAND.circ as structural Verilog: 1 circuit, main circuit main
module main (
  input  VinA,
  input  VinB,
  input  VinC,
  output out_4
);

  wire nand_1_out, nand_2_out, nand_3_out, nand_4_out, nand_5_out, nand_6_out, nand_7_out, nand_8_out;

  nand nand_1 (nand_1_out, VinA, VinA);
  nand nand_2 (nand_2_out, VinB, VinC);
  nand nand_3 (nand_3_out, nand_1_out, VinB);
  nand nand_4 (nand_4_out, VinC, VinC);
  nand nand_5 (nand_5_out, VinB, nand_2_out);
  nand nand_6 (nand_6_out, nand_3_out, nand_3_out);
  nand nand_7 (nand_7_out, nand_6_out, nand_4_out);
  nand nand_8 (nand_8_out, VinA, nand_5_out);
  nand nand_9 (out_4, nand_7_out, nand_8_out);
endmodule
