// Logisim project FurnaceControl.circ as structural Verilog: 1 circuit, main circuit main
module main (
  input  VinA,
  input  VinB,
  input  VinC,
  input  VinD,
  output GasShutOff,
  output FaultySensor
);

  wire and_1_out, and_2_out, and_3_out, and_4_out, and_5_out, and_6_out, and_7_out, and_8_out, and_9_out,
       and_10_out, not_1_out, not_2_out, not_3_out, not_4_out, or_1_out, or_2_out, or_4_out;

  or or_1 (or_1_out, VinC, VinD);
  and and_1 (and_1_out, VinA, VinB);
  and and_2 (and_2_out, VinC, VinD);
  or or_2 (or_2_out, VinB, VinA);
  and and_3 (and_3_out, VinA, VinB);
  and and_4 (and_4_out, VinC, VinD);
  not not_1 (not_1_out, VinA);
  and and_5 (and_5_out, not_1_out, not_2_out);
  not not_2 (not_2_out, VinB);
  not not_3 (not_3_out, VinC);
  and and_6 (and_6_out, not_3_out, not_4_out);
  not not_4 (not_4_out, VinD);
  and and_7 (and_7_out, or_1_out, and_1_out);
  and and_8 (and_8_out, and_2_out, or_2_out);
  and and_9 (and_9_out, and_3_out, and_4_out);
  and and_10 (and_10_out, and_5_out, and_6_out);
  or or_3 (GasShutOff, and_7_out, and_8_out);
  or or_4 (or_4_out, and_9_out, and_10_out);
  not not_5 (FaultySensor, or_4_out);
endmodule
