// Logisim project LoadProgrammable.circ as structural Verilog: 2 circuits, main circuit main
module main (
);

  wire and_1_out, clock_1_out, dipswitch_2_sw1, dipswitch_2_sw2, dipswitch_2_sw3, dipswitch_2_sw4, not_1_out,
       not_2_out, not_3_out, not_4_out, xor_1_out, xor_2_out, xor_3_out, xor_4_out;
  wire [3:0] counter_1_q, dipswitch_1_sw4;

  Clock clock_1 (.out(clock_1_out));
  DipSwitch #(.number(4)) dipswitch_1 (
    .sw1(dipswitch_1_sw4[3]), .sw2(dipswitch_1_sw4[2]), .sw3(dipswitch_1_sw4[1]), .sw4(dipswitch_1_sw4[0]));
  Counter #(.max('hf), .width(4)) counter_1 (
    .load(and_1_out), .D(dipswitch_1_sw4), .count(1'b1), .Q(counter_1_q), .up(1'b1), .clk(clock_1_out));  // open: carry, clr
  xor xor_1 (xor_1_out, dipswitch_2_sw1, counter_1_q[3]);
  xor xor_2 (xor_2_out, dipswitch_2_sw2, counter_1_q[2]);
  not not_1 (not_1_out, xor_1_out);
  not not_2 (not_2_out, xor_2_out);
  xor xor_3 (xor_3_out, dipswitch_2_sw3, counter_1_q[1]);
  not not_3 (not_3_out, xor_3_out);
  and and_1 (and_1_out, not_1_out, not_2_out, not_3_out, not_4_out);
  xor xor_4 (xor_4_out, dipswitch_2_sw4, counter_1_q[0]);
  not not_4 (not_4_out, xor_4_out);
  DipSwitch #(.number(4)) dipswitch_2 (
    .sw1(dipswitch_2_sw1), .sw2(dipswitch_2_sw2), .sw3(dipswitch_2_sw3), .sw4(dipswitch_2_sw4));
  Hex_Digit_Display hex_digit_display_1 (.value(counter_1_q));  // open: dp
  // Digital_Oscilloscope digital_oscilloscope_1: pin names not known; wires that end beside it: clock_1_out, counter_1_q[0], counter_1_q[1], counter_1_q[2], counter_1_q[3], 1'b1
endmodule

module DoubleTime (
);

  wire and_1_out, clock_1_out, dipswitch_2_sw1, dipswitch_2_sw2, dipswitch_2_sw3, dipswitch_2_sw4, not_1_out,
       not_2_out, not_3_out, not_4_out, xor_1_out, xor_2_out, xor_3_out, xor_4_out;
  wire [3:0] counter_1_q, dipswitch_1_sw4;

  Clock clock_1 (.out(clock_1_out));
  DipSwitch #(.number(4)) dipswitch_1 (
    .sw1(dipswitch_1_sw4[3]), .sw2(dipswitch_1_sw4[2]), .sw3(dipswitch_1_sw4[1]), .sw4(dipswitch_1_sw4[0]));
  Counter #(.max('hf), .width(4)) counter_1 (
    .load(and_1_out), .D(dipswitch_1_sw4), .count(1'b1), .Q(counter_1_q), .up(1'b1), .clk(clock_1_out));  // open: carry, clr
  xor xor_1 (xor_1_out, dipswitch_2_sw1, counter_1_q[3]);
  xor xor_2 (xor_2_out, dipswitch_2_sw2, counter_1_q[2]);
  not not_1 (not_1_out, xor_1_out);
  not not_2 (not_2_out, xor_2_out);
  xor xor_3 (xor_3_out, dipswitch_2_sw3, counter_1_q[1]);
  not not_3 (not_3_out, xor_3_out);
  and and_1 (and_1_out, not_1_out, not_2_out, not_3_out, not_4_out);
  xor xor_4 (xor_4_out, dipswitch_2_sw4, counter_1_q[0]);
  not not_4 (not_4_out, xor_4_out);
  DipSwitch #(.number(4)) dipswitch_2 (
    .sw1(dipswitch_2_sw1), .sw2(dipswitch_2_sw2), .sw3(dipswitch_2_sw3), .sw4(dipswitch_2_sw4));
  Hex_Digit_Display hex_digit_display_1 (.value(counter_1_q));  // open: dp
  // Digital_Oscilloscope digital_oscilloscope_1: pin names not known; wires that end beside it: clock_1_out, counter_1_q[0], counter_1_q[1], counter_1_q[2], counter_1_q[3], 1'b1
endmodule
