// Logisim project SMA1.circ as structural Verilog: 1 circuit, main circuit clock_edge
module clock_edge (
  input  E,
  output vOut
);

  wire and_1_out, and_2_out, and_3_out, and_4_out, clock_1_out, or_1_out, or_2_out, or_3_out, Qa_q, Qb_q,
       Qb_qn;

  Clock clock_1 (.out(clock_1_out));
  and and_1 (and_1_out, Qa_q, Qb_qn);
  and and_2 (and_2_out, E, Qb_q);
  D_Flip_Flop Qa (.D(or_1_out), .clk(clock_1_out), .Q(Qa_q));  // open: Qn, preset, reset
  or or_1 (or_1_out, and_1_out, and_2_out);
  or or_2 (or_2_out, E, Qa_q);
  and and_3 (and_3_out, or_2_out, Qb_qn);
  and and_4 (and_4_out, Qa_q, E);
  D_Flip_Flop Qb (.D(or_3_out), .clk(clock_1_out), .Q(Qb_q), .Qn(Qb_qn));  // open: preset, reset
  or or_3 (or_3_out, and_3_out, and_4_out);
  // Digital_Oscilloscope digital_oscilloscope_1: pin names not known; wires that end beside it: clock_1_out, E, Qa_q, Qb_q, vOut, 1'b1
  and and_5 (vOut, Qb_qn, Qa_q);
endmodule
