// Logisim project SSDproject.circ as structural Verilog: 10 circuits, main circuit main
module main (
);

  wire a_1_sega, b_1_segb, c_1_segc, d_1_segd, e_1_sege, f_1_segf, g_1_segg;
  wire [2:0] timerjk_1_out_1;

  TimerJK timerjk_1 (.out_1(timerjk_1_out_1));
  A a_1 (.Sel(timerjk_1_out_1), .SegA(a_1_sega));
  B b_1 (.Sel(timerjk_1_out_1), .SegB(b_1_segb));
  C c_1 (.Sel(timerjk_1_out_1), .SegC(c_1_segc));
  D d_1 (.Sel(timerjk_1_out_1), .SegD(d_1_segd));
  E e_1 (.Sel(timerjk_1_out_1), .SegE(e_1_sege));
  F f_1 (.Sel(timerjk_1_out_1), .SegF(f_1_segf));
  G g_1 (.Sel(timerjk_1_out_1), .SegG(g_1_segg));
  _7_Segment_Display u_7_segment_display_1 (
    .g(g_1_segg), .f(f_1_segf), .a(a_1_sega), .b(b_1_segb), .e(e_1_sege), .d(d_1_segd), .c(c_1_segc));  // open: dp
endmodule

module A (
  input  [2:0] Sel,
  output SegA
);

  wire nand_1_out, nand_2_out, nand_3_out, nand_4_out, nand_5_out, nand_6_out;

  nand nand_1 (nand_1_out, Sel[2], Sel[2]);
  nand nand_2 (nand_2_out, Sel[0], Sel[0]);
  nand nand_3 (nand_3_out, Sel[1], Sel[1]);
  nand nand_4 (nand_4_out, nand_1_out, nand_2_out);
  nand nand_5 (nand_5_out, nand_4_out, Sel[1]);
  nand nand_6 (nand_6_out, nand_2_out, nand_3_out);
  nand nand_7 (SegA, nand_5_out, nand_6_out);
endmodule

module B (
  input  [2:0] Sel,
  output SegB
);

  wire nor_1_out, nor_2_out, nor_3_out, nor_4_out, nor_5_out, nor_6_out, nor_7_out, nor_8_out;

  nor nor_1 (nor_1_out, Sel[1], Sel[1]);
  nor nor_2 (nor_2_out, Sel[2], Sel[2]);
  nor nor_3 (nor_3_out, Sel[0], nor_1_out);
  nor nor_4 (nor_4_out, nor_3_out, Sel[2]);
  nor nor_5 (nor_5_out, nor_6_out, nor_6_out);
  nor nor_6 (nor_6_out, nor_1_out, nor_2_out);
  nor nor_7 (nor_7_out, Sel[0], nor_5_out);
  nor nor_8 (nor_8_out, nor_4_out, nor_7_out);
  nor nor_9 (SegB, nor_8_out, nor_8_out);
endmodule

module C (
  input  [2:0] Sel,
  output SegC
);

  wire and_1_out, and_2_out, nor_1_out, not_1_out, or_1_out;

  not not_1 (not_1_out, Sel[0]);
  and and_1 (and_1_out, not_1_out, Sel[2]);
  and and_2 (and_2_out, Sel[0], Sel[1]);
  nor nor_1 (nor_1_out, Sel[1], Sel[2]);
  or or_1 (or_1_out, and_1_out, and_2_out);
  or or_2 (SegC, or_1_out, nor_1_out);
endmodule

module D (
  input  [2:0] Sel,
  output SegD
);

  wire and_1_out, nor_1_out, or_1_out;

  nor nor_1 (nor_1_out, Sel[0], Sel[1]);
  and and_1 (and_1_out, Sel[1], or_1_out);
  or or_1 (or_1_out, Sel[0], Sel[2]);
  or or_2 (SegD, nor_1_out, and_1_out);
endmodule

module E (
  input  [2:0] Sel,
  output SegE
);

  wire and_1_out, and_2_out, and_3_out, nor_1_out, not_1_out, not_2_out, or_1_out;

  nor nor_1 (nor_1_out, Sel[0], Sel[1]);
  and and_1 (and_1_out, Sel[0], Sel[1]);
  not not_1 (not_1_out, Sel[0]);
  and and_2 (and_2_out, not_1_out, Sel[2]);
  or or_1 (or_1_out, nor_1_out, and_1_out);
  not not_2 (not_2_out, Sel[2]);
  and and_3 (and_3_out, or_1_out, not_2_out);
  or or_2 (SegE, and_3_out, and_2_out);
endmodule

module F (
  input  [2:0] Sel,
  output SegF
);

  wire and_1_out, and_2_out, nor_1_out, not_1_out, or_1_out;

  not not_1 (not_1_out, Sel[0]);
  and and_1 (and_1_out, not_1_out, Sel[2]);
  and and_2 (and_2_out, Sel[0], Sel[1]);
  nor nor_1 (nor_1_out, Sel[1], Sel[2]);
  or or_1 (or_1_out, and_1_out, and_2_out);
  or or_2 (SegF, or_1_out, nor_1_out);
endmodule

module G (
  input  [2:0] Sel,
  output SegG
);

  wire and_1_out, and_2_out, and_3_out, and_4_out, not_1_out, not_2_out, not_3_out, or_1_out, or_2_out;

  not not_1 (not_1_out, Sel[2]);
  and and_1 (and_1_out, Sel[0], Sel[2]);
  not not_2 (not_2_out, Sel[1]);
  or or_1 (or_1_out, Sel[0], Sel[2]);
  and and_2 (and_2_out, not_1_out, Sel[1]);
  not not_3 (not_3_out, Sel[0]);
  or or_2 (or_2_out, and_1_out, and_3_out);
  and and_3 (and_3_out, not_2_out, or_1_out);
  and and_4 (and_4_out, and_2_out, not_3_out);
  or or_3 (SegG, or_2_out, and_4_out);
endmodule

module TimerDFF (
  output [2:0] out_1
);

  wire and_1_out, and_2_out, and_3_out, clock_1_out, d_ff_1_q, d_ff_2_q, d_ff_3_q, or_1_out, xor_1_out;

  Clock clock_1 (.out(clock_1_out));
  D_Flip_Flop d_ff_1 (.D(out_1[0]), .clk(clock_1_out), .Q(d_ff_1_q), .Qn(out_1[0]));  // open: preset, reset
  and and_1 (and_1_out, d_ff_3_q, out_1[1]);
  and and_2 (and_2_out, d_ff_3_q, out_1[0]);
  and and_3 (and_3_out, out_1[2], d_ff_1_q, d_ff_2_q);
  D_Flip_Flop d_ff_2 (.D(xor_1_out), .clk(clock_1_out), .Q(d_ff_2_q), .Qn(out_1[1]));  // open: preset, reset
  or or_1 (or_1_out, and_1_out, and_2_out, and_3_out);
  xor xor_1 (xor_1_out, d_ff_1_q, d_ff_2_q);
  D_Flip_Flop d_ff_3 (.D(or_1_out), .clk(clock_1_out), .Q(d_ff_3_q), .Qn(out_1[2]));  // open: preset, reset
endmodule

module TimerJK (
  output [2:0] out_1
);

  wire and_1_out, clock_1_out;

  Clock clock_1 (.out(clock_1_out));
  and and_1 (and_1_out, out_1[0], out_1[1]);
  J_K_Flip_Flop j_k_ff_1 (
    .J(and_1_out), .K(and_1_out), .clk(clock_1_out), .Q(out_1[2]), .preset(1'b0), .reset(1'b0));  // open: Qn
  J_K_Flip_Flop j_k_ff_2 (
    .J(out_1[0]), .K(out_1[0]), .clk(clock_1_out), .Q(out_1[1]), .preset(1'b0), .reset(1'b0));  // open: Qn
  J_K_Flip_Flop j_k_ff_3 (
    .J(1'b1), .K(1'b1), .clk(clock_1_out), .Q(out_1[0]), .preset(1'b0), .reset(1'b0));  // open: Qn
endmodule
